# Fritzing sketch sketch (saved by Fritzing 0.9.2b)
breadboards: 3

parts:
  Part1 = Arduino Uno (Rev3)
  LCD1 = LCD screen
  R1 = Resistor [tolerance=±5% resistance=220 package="2010 [SMD]"]
  R2 = Trimmer Potentiometer [maximum_resistance=10kΩ package=THT]
  Part2 = Triple Axis Accelerometer Breakout - ADXL345
  S1 = Momentary Switch [package=ksa_sealed_tac_switch]
  R3 = Resistor [tolerance=±5% resistance=10k package="2512 [SMD]"]
  R4 = Resistor [tolerance=±5% resistance=10k package="2512 [SMD]"]

nets:
  N1: Part1.A4/SDA, Part2.SDA, R3.Pin_1
  N2: Part1.A5/SCL, Part2.SCL, R4.Pin_1
  N3: Part1.D8, S1.2
  N4: Part1.D2, LCD1.DB7
  N5: Part1.D3_PWM, LCD1.DB6
  N6: Part1.D4, LCD1.DB5
  N7: Part1.D5_PWM, LCD1.DB4
  N8: Part1.D6_PWM, LCD1.E
  N9: Part1.D7, LCD1.RS
  3V3: Part1.3V3, Part2.VCC, Part2.CS, R3.Pin_0, R4.Pin_0
  5V: Part1.5V, LCD1.VDD, R1.Pin_0, R2.leg2, S1.3
  GND: Part1.GND, LCD1.VSS, LCD1.R/W, LCD1.LED-, R2.leg1, Part2.GND, Part2.SDO, S1.1
  N10: LCD1.V0, R2.wiper
  N11: LCD1.LED+, R1.Pin_1
